// Logisim project Processor.circ as structural Verilog
module main (
);

  Register_File register_file_1 ();  // open: D, Rw, W, Ra, Rb, Qb
endmodule

// rising
module Register_File (
  input  [31:0] D,
  input  [4:0] Rw,
  input  W,
  input  [4:0] Ra,
  input  [4:0] Rb,
  output [31:0] Qb
);

  wire and_1_out, and_2_out, and_3_out, and_4_out, and_5_out, and_7_out, and_8_out, and_9_out, and_10_out,
       and_11_out, and_12_out, and_13_out, and_14_out, and_15_out, and_16_out, and_17_out, and_19_out,
       and_20_out, and_21_out, and_22_out, and_23_out, and_24_out, and_25_out, and_27_out, and_28_out,
       and_29_out, and_30_out, and_32_out, and_33_out, clock_1_out, counter_1_p1, undriven, undriven_2,
       undriven_3, undriven_4, undriven_5, undriven_6, undriven_7, undriven_8, undriven_9, undriven_10,
       undriven_11, undriven_12, undriven_13, undriven_14, undriven_15, undriven_16, undriven_17,
       undriven_18, undriven_19, undriven_20, undriven_21, undriven_22, undriven_23, undriven_24,
       undriven_26, undriven_27, undriven_28, undriven_29, undriven_30, undriven_31, undriven_32,
       undriven_33, undriven_35;
  wire [31:0] _0_q, _1_q, _2_q, _3_q, _4_q, _5_q, _7_q, _8_q, _9_q, _10_q, _11_q, _12_q, _13_q, _14_q, _15_q,
       _16_q, _17_q, _18_q, _19_q, _20_q, _21_q, _22_q, _23_q, _24_q, _26_q, _27_q, _28_q, _29_q, _31_2_q,
       _31_q, multiplexer_1_out, undriven_25, undriven_34;

  Clock clock_1 (.out(clock_1_out));
  and and_1 (and_1_out, W, undriven);
  and and_2 (and_2_out, W, undriven_2);
  and and_3 (and_3_out, W, undriven_3);
  and and_4 (and_4_out, W, undriven_4);
  and and_5 (and_5_out, W, undriven_5);
  // AND_Gate and_6 has open pins: in0=W, in1=undriven_6, out=open
  and and_7 (and_7_out, W, undriven_7);
  // Counter counter_1: pin names not known; wires that end beside it: counter_1_p1
  Register #(.width(32)) _0 (.en(counter_1_p1), .Q(_0_q));  // open: D, clk, clr
  Register #(.width(32)) _1 (.D(D), .en(and_1_out), .Q(_1_q), .clk(clock_1_out));  // open: clr
  Register #(.width(32)) _2 (.D(D), .en(and_2_out), .Q(_2_q), .clk(clock_1_out));  // open: clr
  Register #(.width(32)) _3 (.D(D), .en(and_3_out), .Q(_3_q), .clk(clock_1_out));  // open: clr
  Register #(.width(32)) _4 (.D(D), .en(and_4_out), .Q(_4_q), .clk(clock_1_out), .clr(undriven_20));
  Register #(.width(32)) _4_2 (.D(D), .en(and_4_out), .Q(_4_q), .clk(clock_1_out), .clr(undriven_20));
  Register #(.width(32)) _5 (.D(D), .en(and_5_out), .Q(_5_q), .clk(clock_1_out));  // open: clr
  Register #(.width(32)) _7 (.D(D), .en(and_7_out), .Q(_7_q), .clk(clock_1_out));  // open: clr
  and and_8 (and_8_out, W, undriven_21);
  and and_9 (and_9_out, W, undriven_22);
  and and_10 (and_10_out, W, undriven_23);
  and and_11 (and_11_out, W, undriven_8);
  and and_12 (and_12_out, W, undriven_9);
  and and_13 (and_13_out, W, undriven_24);
  and and_14 (and_14_out, W, undriven_26);
  and and_15 (and_15_out, W, undriven_27);
  Register #(.width(32)) _8 (.D(D), .en(and_8_out), .Q(_8_q), .clk(clock_1_out));  // open: clr
  Register #(.width(32)) _9 (.D(D), .en(and_9_out), .Q(_9_q), .clk(clock_1_out));  // open: clr
  Register #(.width(32)) _10 (.D(D), .en(and_10_out), .Q(_10_q), .clk(clock_1_out));  // open: clr
  Register #(.width(32)) _11 (.D(D), .en(and_11_out), .Q(_11_q), .clk(clock_1_out));  // open: clr
  Register #(.width(32)) _12 (.D(D), .en(and_12_out), .Q(_12_q), .clk(clock_1_out));  // open: clr
  Register #(.width(32)) _13 (.D(D), .en(and_13_out), .Q(_13_q), .clk(clock_1_out), .clr(undriven_28));
  Register #(.width(32)) _13_2 (.D(D), .en(and_13_out), .Q(_13_q), .clk(clock_1_out), .clr(undriven_28));
  Register #(.width(32)) _14 (.D(D), .en(and_14_out), .Q(_14_q), .clk(clock_1_out));  // open: clr
  Register #(.width(32)) _15 (.D(D), .en(and_15_out), .Q(_15_q), .clk(clock_1_out));  // open: clr
  and and_16 (and_16_out, W, undriven_29);
  and and_17 (and_17_out, W, undriven_30);
  and and_18 (and_17_out, W, undriven_30);
  and and_19 (and_19_out, W, undriven_10);
  and and_20 (and_20_out, W, undriven_11);
  and and_21 (and_21_out, W, undriven_12);
  and and_22 (and_22_out, W, undriven_31);
  and and_23 (and_23_out, W, undriven_32);
  and and_24 (and_24_out, W, undriven_13);
  Register #(.width(32)) _16 (.D(D), .en(and_16_out), .Q(_16_q), .clk(clock_1_out));  // open: clr
  Register #(.width(32)) _17 (.D(D), .en(and_17_out), .Q(_17_q), .clk(clock_1_out));  // open: clr
  Register #(.width(32)) _18 (.D(D), .en(and_19_out), .Q(_18_q), .clk(clock_1_out));  // open: clr
  Register #(.width(32)) _19 (.D(D), .en(and_20_out), .Q(_19_q), .clk(clock_1_out));  // open: clr
  Register #(.width(32)) _20 (.D(D), .en(and_21_out), .Q(_20_q), .clk(clock_1_out));  // open: clr
  Register #(.width(32)) _21 (.D(D), .en(and_22_out), .Q(_21_q), .clk(clock_1_out));  // open: clr
  Register #(.width(32)) _22 (.D(D), .en(and_23_out), .Q(_22_q), .clk(clock_1_out));  // open: clr
  Register #(.width(32)) _23 (.D(D), .en(and_24_out), .Q(_23_q), .clk(clock_1_out));  // open: clr
  and and_25 (and_25_out, W, W);
  // AND_Gate and_26 has open pins: in0=W, in1=undriven_14, out=open
  and and_27 (and_27_out, W, undriven_15);
  and and_28 (and_28_out, W, undriven_16);
  and and_29 (and_29_out, W, undriven_17);
  and and_30 (and_30_out, W, undriven_18);
  and and_31 (and_30_out, W, undriven_18);
  and and_32 (and_32_out, W, undriven_33);
  and and_33 (and_33_out, W, undriven_19);
  Register #(.width(32)) _24 (.D(D), .en(and_25_out), .Q(_24_q), .clk(clock_1_out));  // open: clr
  Register #(.width(32)) _26 (.D(D), .en(and_27_out), .Q(_26_q), .clk(clock_1_out));  // open: clr
  Register #(.width(32)) _27 (.D(D), .en(and_28_out), .Q(_27_q), .clk(clock_1_out));  // open: clr
  Register #(.width(32)) _28 (.D(D), .en(and_29_out), .Q(_28_q), .clk(clock_1_out), .clr(undriven_35));
  Register #(.width(32)) _28_2 (.D(D), .en(and_29_out), .Q(_28_q), .clk(clock_1_out), .clr(undriven_35));
  Register #(.width(32)) _29 (.D(D), .en(and_30_out), .Q(_29_q), .clk(clock_1_out));  // open: clr
  Register #(.width(32)) _31 (.D(D), .en(and_32_out), .Q(_31_q), .clk(clock_1_out));  // open: clr
  Register #(.width(32)) _31_2 (.D(D), .en(and_33_out), .Q(_31_2_q), .clk(clock_1_out));  // open: clr
  Multiplexer #(.select(5), .width(32), .enable("false")) multiplexer_1 (
    .in0(_0_q), .in1(_1_q), .in2(_2_q), .in3(_3_q), .in4(_4_q), .in5(_5_q), .in6(undriven_25), .in7(_7_q),
    .in8(_8_q), .in9(_9_q), .in10(_10_q), .in11(_11_q), .in12(_12_q), .in13(_13_q), .in14(_14_q),
    .in15(_15_q), .in16(_16_q), .in17(_17_q), .in18(_18_q), .in19(_19_q), .in20(_20_q), .in21(_21_q),
    .in22(_22_q), .in23(_23_q), .in24(_24_q), .in25(undriven_34), .in26(_26_q), .in27(_27_q), .in28(_28_q),
    .in29(_29_q), .in30(_31_q), .in31(_31_2_q), .out(multiplexer_1_out), .sel(Ra));
  Multiplexer #(.select(5), .width(32), .enable("false")) multiplexer_2 (
    .in0(_0_q), .in1(_1_q), .in2(_2_q), .in3(_3_q), .in4(_4_q), .in5(_5_q), .in6(undriven_25), .in7(_7_q),
    .in8(_8_q), .in9(_9_q), .in10(_10_q), .in11(_11_q), .in12(_12_q), .in13(_13_q), .in14(_14_q),
    .in15(_15_q), .in16(_16_q), .in17(_17_q), .in18(_18_q), .in19(_19_q), .in20(_20_q), .in21(_21_q),
    .in22(_22_q), .in23(_23_q), .in24(_24_q), .in25(undriven_34), .in26(_26_q), .in27(_27_q), .in28(_28_q),
    .in29(_29_q), .in30(_31_q), .in31(_31_2_q), .out(Qb), .sel(Rb));
endmodule
